# Fritzing sketch STTF2013_Fritzing_Cyclists (saved by Fritzing 0.7.11b)
breadboards: 1

parts:
  LED1 = 8x8 LED Matrix (red)
  FET1 = STP16NF06 N-Channel Power MOSFET
  R1 = Resistor [tolerance=±5% resistance=220 package=THT]
  R2 = Resistor [tolerance=±5% resistance=220 package=THT]
  R3 = Resistor [tolerance=±5% resistance=220 package=THT]
  Arduino1 = Arduino
  S2 = Round Pushbutton
  LED2 = smd LED [color="Red (633nm)" package="1206 [SMD]"]
  Parte1 = Gas Sensor Breakout Board
  J1 = Peltier Element

nets:
  N1: LED1.+, Arduino1.+5V, Parte1.A1, Parte1.A2, Parte1.H1
  N2: LED1.-, FET1.source, R3.Pin_1, LED2.cathode, Parte1.GND
  N3: LED1.D, Arduino1.A4
  N4: LED1.C, Arduino1.A5
  N5: FET1.gate, R1.Pin_1, Arduino1.D3, LED2.anode
  N6: FET1.drain, J1.pin1
  N7: R2.Pin_0, S2.leg0
  N8: R3.Pin_0, Parte1.B2
  N9: Arduino1.D7, S2.leg1
  N10: Arduino1.A0, Parte1.B1

custom parts:
  8x8 LED Matrix (red): 8x8 LED Matrix with I2C control (red)
  STP16NF06 N-Channel Power MOSFET: STP16NF06 N-channel Power MOSFET
